# Fritzing sketch esp-media-control (saved by Fritzing 0.9.5d)

parts:
  M1 = ESP32-S3-DevKitC-1-N8R8-v1 [part_number=ESP32-S3-DevKitC-1-N8R8-v1]
  U1 = POT [package=pot_alpha_rv16af-20]
  S1 = Pushbutton [package="[SMD]"]
  S2 = Pushbutton [package="[SMD]"]
  S3 = Pushbutton [package="[SMD]"]
  C1 = Ceramic Capacitor [capacitance="100 nF" package="0603 [SMD, multilayer]"]

nets:
  N1: M1.pin_1, M1.pin_2, U1.A
  N2: M1.pin_16, S1.Pin_3, S1.Pin_4
  N3: M1.pin_17, S2.Pin_3, S2.Pin_4
  N4: M1.pin_18, S3.Pin_3, S3.Pin_4
  N5: M1.pin_22, M1.pin_23, M1.pin_24, M1.pin_44, U1.E, S1.Pin_2, S2.Pin_1, S2.Pin_2, S3.Pin_2, C1.0
  N6: M1.pin_41, U1.S

custom parts:
  ESP32-S3-DevKitC-1-N8R8-v1: ESP32-S3-DevKitC-1-N8R8-v1 This module is 44pins long (2x22) and 11 pins width.
